// Logisim project projet Logique-Circuit.circ as structural Verilog: 12 circuits, main circuit main
module main (
  input  _0,
  input  _0_2,
  input  _1,
  input  _1_2,
  input  _2,
  input  _2_2,
  input  _3,
  input  _3_2,
  input  _4,
  input  _4_2,
  input  _5,
  input  _5_2,
  input  _0_3,
  input  _0_4,
  input  _0_5,
  input  _1_3,
  input  _1_4,
  input  _1_5,
  input  _2_3,
  input  _2_4,
  input  _2_5,
  input  RESET,
  input  _3_3,
  input  _3_4,
  input  _0_6,
  input  _4_3,
  input  _4_4,
  input  _1_6,
  input  _5_3,
  input  _5_4,
  input  _2_6,
  input  _6,
  input  _6_2,
  input  _3_5,
  input  _7,
  input  _7_2,
  input  _4_5,
  input  _8,
  input  _8_2,
  input  _5_5,
  input  _9,
  input  _9_2,
  input  _6_3,
  input  _7_3,
  input  _8_3,
  input  _9_3
);

  wire and_1_out, circuit_d_heure_1_e1_e2, circuit_de_controle_1_nq, circuit_de_controle_1_q,
       circuit_de_seconde_et_minute_1_e1_e2, circuit_de_seconde_et_minute_1_output_pour_la_seconde_circuit,
       circuit_de_seconde_et_minute_2_e1_e2, circuit_de_seconde_et_minute_2_output_pour_la_seconde_circuit,
       clock_1_out;
  wire [3:0] circuit_d_heure_1_screen1, circuit_d_heure_1_screen2, circuit_de_seconde_et_minute_1_screen1,
       circuit_de_seconde_et_minute_1_screen2, circuit_de_seconde_et_minute_2_screen1,
       circuit_de_seconde_et_minute_2_screen2;

  circuit_de_Controle circuit_de_controle_1 (
    .Resultat_de_multiplication_des_comparateurs(and_1_out), .RESET_for_ALARME(RESET),
    .Q(circuit_de_controle_1_q), .nQ(circuit_de_controle_1_nq));
  Hex_Digit_Display hex_digit_display_1 (.value(circuit_d_heure_1_screen2));  // open: dp
  Hex_Digit_Display hex_digit_display_2 (.value(circuit_d_heure_1_screen1));  // open: dp
  circuit_d_heure circuit_d_heure_1 (
    .nqControl(circuit_de_controle_1_nq),
    .CLK(circuit_de_seconde_et_minute_1_output_pour_la_seconde_circuit), .qControl(circuit_de_controle_1_q),
    .screen2(circuit_d_heure_1_screen2), .screen1(circuit_d_heure_1_screen1), .in_4(_0_5), .in_5(_1_5),
    .in_6(_2_3), .in_7(_0_6), .in_8(_1_6), .in_9(_2_6), .in_10(_3_5), .in_11(_4_5), .in_12(_5_5),
    .in_13(_6_3), .in_14(_7_3), .in_15(_8_3), .in_16(_9_3), .e1_e2(circuit_d_heure_1_e1_e2));
  and and_1 (and_1_out, circuit_d_heure_1_e1_e2, circuit_de_seconde_et_minute_1_e1_e2, circuit_de_seconde_et_minute_2_e1_e2);
  LED led_1 (.in(circuit_de_controle_1_q));
  LED led_2 (.in(circuit_de_controle_1_q));
  Hex_Digit_Display hex_digit_display_3 (.value(circuit_de_seconde_et_minute_1_screen2));  // open: dp
  Hex_Digit_Display hex_digit_display_4 (.value(circuit_de_seconde_et_minute_1_screen1));  // open: dp
  circuit_de_seconde_et_minute circuit_de_seconde_et_minute_1 (
    .output_pour_la_seconde_circuit(circuit_de_seconde_et_minute_1_output_pour_la_seconde_circuit),
    .CLK(circuit_de_seconde_et_minute_2_output_pour_la_seconde_circuit),
    .nqcontrole1(circuit_de_controle_1_nq), .qcontrole1(circuit_de_controle_1_q), ._0(_0), .in_6(_1),
    .in_8(_2), .in_9(_3), .in_10(_4), .in_11(_5), .in_12(_0_3), .in_13(_1_3), .in_14(_2_4), .in_15(_3_3),
    .in_16(_4_3), .in_17(_5_3), .in_18(_6), .in_19(_7), ._8(_8), .in_21(_9),
    .screen2(circuit_de_seconde_et_minute_1_screen2), .screen1(circuit_de_seconde_et_minute_1_screen1),
    .nqcontrole2(circuit_de_controle_1_nq), .qcontrole2(circuit_de_controle_1_q),
    .e1_e2(circuit_de_seconde_et_minute_1_e1_e2));
  LED led_3 (.in(circuit_de_controle_1_q));
  LED led_4 (.in(circuit_de_controle_1_q));
  Clock clock_1 (.out(clock_1_out));
  Hex_Digit_Display hex_digit_display_5 (.value(circuit_de_seconde_et_minute_2_screen2));  // open: dp
  Hex_Digit_Display hex_digit_display_6 (.value(circuit_de_seconde_et_minute_2_screen1));  // open: dp
  circuit_de_seconde_et_minute circuit_de_seconde_et_minute_2 (
    .output_pour_la_seconde_circuit(circuit_de_seconde_et_minute_2_output_pour_la_seconde_circuit),
    .CLK(clock_1_out), .nqcontrole1(circuit_de_controle_1_nq), .qcontrole1(circuit_de_controle_1_q),
    ._0(_0_2), .in_6(_1_2), .in_8(_2_2), .in_9(_3_2), .in_10(_4_2), .in_11(_5_2), .in_12(_0_4), .in_13(_1_4),
    .in_14(_2_5), .in_15(_3_4), .in_16(_4_4), .in_17(_5_4), .in_18(_6_2), .in_19(_7_2), ._8(_8_2),
    .in_21(_9_2), .screen2(circuit_de_seconde_et_minute_2_screen2),
    .screen1(circuit_de_seconde_et_minute_2_screen1), .nqcontrole2(circuit_de_controle_1_nq),
    .qcontrole2(circuit_de_controle_1_q), .e1_e2(circuit_de_seconde_et_minute_2_e1_e2));
  LED led_5 (.in(circuit_de_controle_1_q));
  LED led_6 (.in(circuit_de_controle_1_q));

  // Notes on the sheet:
  //   H2
  //   H1
  //   M2
  //   M1
  //   H2H1:M2M1:S2S1, Pour l'Alarme
  //   S2
  //   S1
endmodule

module compteur_synchrone_modulo_10 (
  input  RESET,
  input  CLK,
  output q2_10,
  output q1_10,
  output q3_10,
  output q0_10,
  output nq0_10,
  output nq1_10,
  output nq2_10,
  output nq2_10_2
);

  wire and_1_out, and_2_out, and_3_out, and_4_out, or_1_out;

  J_K_Flip_Flop j_k_ff_1 (.J(1'b1), .clk(CLK), .K(1'b1), .Q(q0_10), .Qn(nq0_10), .reset(RESET));  // open: preset, en
  and and_1 (and_1_out, nq2_10_2, q0_10);
  J_K_Flip_Flop j_k_ff_2 (
    .J(and_1_out), .clk(CLK), .K(and_1_out), .Q(q1_10), .Qn(nq1_10), .reset(RESET));  // open: preset, en
  and and_2 (and_2_out, q0_10, q1_10);
  J_K_Flip_Flop j_k_ff_3 (
    .J(and_2_out), .clk(CLK), .K(and_2_out), .Q(q2_10), .Qn(nq2_10), .reset(RESET));  // open: preset, en
  and and_3 (and_3_out, q0_10, q1_10, q2_10);
  and and_4 (and_4_out, q0_10, q3_10);
  or or_1 (or_1_out, and_3_out, and_4_out);
  J_K_Flip_Flop j_k_ff_4 (
    .J(or_1_out), .clk(CLK), .K(or_1_out), .Q(q3_10), .Qn(nq2_10_2), .reset(RESET));  // open: preset, en
endmodule

module compteur_synchrone_modulo_6 (
  input  CLK,
  output q0_6,
  output q1_6,
  output q2_6,
  output nq0_6,
  output nq1_6,
  output nq2_6
);

  wire and_1_out, and_2_out, and_3_out, or_1_out;

  J_K_Flip_Flop j_k_ff_1 (.J(1'b1), .clk(CLK), .K(1'b1), .Q(q0_6), .Qn(nq0_6));  // open: preset, en, reset
  and and_1 (and_1_out, q0_6, nq2_6);
  J_K_Flip_Flop j_k_ff_2 (.J(and_1_out), .clk(CLK), .K(and_1_out), .Q(q1_6), .Qn(nq1_6));  // open: preset, en, reset
  and and_2 (and_2_out, q2_6, q0_6);
  and and_3 (and_3_out, q1_6, q0_6);
  or or_1 (or_1_out, and_2_out, and_3_out);
  J_K_Flip_Flop j_k_ff_3 (.J(or_1_out), .clk(CLK), .K(or_1_out), .Q(q2_6), .Qn(nq2_6));  // open: preset, en, reset
endmodule

module comteur_synchrone_modulo_3 (
  input  RESET,
  input  CLK,
  output q0_3,
  output q1_3,
  output nq0_3,
  output nq1_3
);

  J_K_Flip_Flop j_k_ff_1 (.J(1'b1), .clk(CLK), .K(1'b1), .Q(q0_3), .Qn(nq0_3), .reset(RESET));  // open: preset, en
  and and_1 (RESET, q0_3, q1_3);
  J_K_Flip_Flop j_k_ff_2 (.J(q0_3), .clk(CLK), .K(q0_3), .Q(q1_3), .Qn(nq1_3), .reset(RESET));  // open: preset, en
endmodule

module Alaram1 (
  input  q0B,
  input  nqcontrol,
  input  CLK,
  input  qcontrol,
  input  q0encodeur,
  input  q1B,
  input  nqcontrol_2,
  input  CLK_2,
  input  qcontrol_2,
  input  q1encodeur,
  input  q2B,
  input  nqcontrol_3,
  input  CLK_3,
  input  qcontrol_3,
  input  q2encodeur,
  input  q3B,
  input  nqcontrol_4,
  input  CLK_4,
  input  qcontrol_4,
  input  q3encodeur,
  output _0,
  output _1,
  output _2,
  output _3
);

  wire and_1_out, and_2_out, and_3_out, and_4_out, and_5_out, and_6_out, and_7_out, and_8_out;

  and and_1 (and_1_out, q0B, nqcontrol);
  and and_2 (and_2_out, CLK, qcontrol, q0encodeur);
  and and_3 (and_3_out, q1B, nqcontrol_2);
  and and_4 (and_4_out, CLK_2, qcontrol_2, q1encodeur);
  and and_5 (and_5_out, q2B, nqcontrol_3);
  and and_6 (and_6_out, CLK_3, qcontrol_3, q2encodeur);
  and and_7 (and_7_out, q3B, nqcontrol_4);
  and and_8 (and_8_out, CLK_4, qcontrol_4, q3encodeur);
  or or_1 (_0, and_1_out, and_2_out);
  or or_2 (_1, and_3_out, and_4_out);
  or or_3 (_2, and_5_out, and_6_out);
  or or_4 (_3, and_7_out, and_8_out);
endmodule

module Alarm2 (
  input  q0B,
  input  nqcontrol,
  input  CLK,
  input  qcontrol,
  input  q0encodeur,
  input  q1B,
  input  nqcontrol_2,
  input  CLK_2,
  input  qcontrol_2,
  input  q1encodeur,
  input  q2B,
  input  nqcontrol_3,
  input  CLK_3,
  input  qcontrol_3,
  input  q2encodeur,
  output _0,
  output _1,
  output _2
);

  wire and_1_out, and_2_out, and_3_out, and_4_out, and_5_out, and_6_out;

  and and_1 (and_1_out, q0B, nqcontrol);
  and and_2 (and_2_out, CLK, qcontrol, q0encodeur);
  and and_3 (and_3_out, q1B, nqcontrol_2);
  and and_4 (and_4_out, CLK_2, qcontrol_2, q1encodeur);
  and and_5 (and_5_out, q2B, nqcontrol_3);
  and and_6 (and_6_out, CLK_3, qcontrol_3, q2encodeur);
  or or_1 (_0, and_1_out, and_2_out);
  or or_2 (_1, and_3_out, and_4_out);
  or or_3 (_2, and_5_out, and_6_out);
endmodule

module Comparateur_et_Encodeur_1 (
  input  [2:0] in_1,
  input  _0,
  input  _1,
  input  _2,
  input  _3,
  input  _4,
  input  _5,
  input  _0_2,
  input  _1_2,
  input  _2_2,
  input  _3_2,
  input  _4_2,
  input  _5_2,
  input  _6,
  input  _7,
  input  _8,
  input  _9,
  input  [3:0] in_18,
  output q0_5,
  output q1_5,
  output e_5,
  output q2_5,
  output q0_9,
  output q1_9,
  output q2_9,
  output e_9,
  output q3_9
);

  wire or_1_out, or_2_out;
  wire [2:1] priority_encoder_3_out;

  or or_1 (or_1_out, _1_2, _9);
  or or_2 (or_2_out, _8, _9);
  Priority_Encoder priority_encoder_1 (
    .in0(_0), .in1(_1), .in2(_2), .in3(_3), .in4(_4), .in5(_5), .in6(1'b0), .in7(1'b0),
    .out({q2_5, q1_5, q0_5}), .en_in(1'b1));  // open: gs, en_out
  Priority_Encoder priority_encoder_2 (
    .in0(_0_2), .in1(or_1_out), .in2(_2_2), .in3(_3_2), .in4(_4_2), .in5(_5_2), .in6(_6), .in7(_7),
    .out({q2_9, q1_9, q0_9}), .en_in(1'b1));  // open: gs, en_out
  Priority_Encoder priority_encoder_3 (
    .in0(1'b1), .in1(or_2_out), .in2(1'b0), .in3(1'b0), .in4(1'b0), .in5(1'b0), .in6(1'b0), .in7(1'b0),
    .out({priority_encoder_3_out, q3_9}), .en_in(1'b1));  // open: gs, en_out
  Comparator #(.width(3)) comparator_1 (.a({q2_5, q1_5, q0_5}), .b(in_1), .eq(e_5));  // open: gt, lt
  Comparator #(.width(4)) comparator_2 (.a({q3_9, q2_9, q1_9, q0_9}), .b(in_18), .eq(e_9));  // open: gt, lt
endmodule

module Comparateur_et_Encodeur_2 (
  input  [1:0] in_1,
  input  _0,
  input  _1,
  input  _2,
  input  _0_2,
  input  _1_2,
  input  _2_2,
  input  _3,
  input  _4,
  input  _5,
  input  _6,
  input  _7,
  input  _8,
  input  _9,
  input  [3:0] in_15,
  output q0_2,
  output q1_2,
  output e1_e2,
  output q0_9,
  output q1_9,
  output q2_9,
  output q3_9
);

  wire comparator_1_eq, comparator_2_eq, or_1_out, or_2_out;
  wire [2:1] priority_encoder_3_out;
  wire [2:2] priority_encoder_1_out;

  or or_1 (or_1_out, _1_2, _9);
  or or_2 (or_2_out, _8, _9);
  Priority_Encoder priority_encoder_1 (
    .in0(_0), .in1(_1), .in2(_2), .in3(1'b0), .in4(1'b0), .in5(1'b0), .in6(1'b0), .in7(1'b0),
    .out({priority_encoder_1_out[2], q1_2, q0_2}));  // open: en_in, gs, en_out
  Priority_Encoder priority_encoder_2 (
    .in0(_0_2), .in1(or_1_out), .in2(_2_2), .in3(_3), .in4(_4), .in5(_5), .in6(_6), .in7(_7),
    .out({q2_9, q1_9, q0_9}));  // open: en_in, gs, en_out
  Priority_Encoder priority_encoder_3 (
    .in0(1'b1), .in1(or_2_out), .in2(1'b0), .in3(1'b0), .in4(1'b0), .in5(1'b0), .in6(1'b0), .in7(1'b0),
    .out({priority_encoder_3_out, q3_9}));  // open: en_in, gs, en_out
  Comparator #(.width(2)) comparator_1 (.a({q1_2, q0_2}), .b(in_1), .eq(comparator_1_eq));  // open: gt, lt
  Comparator #(.width(4)) comparator_2 (.a({q3_9, q2_9, q1_9, q0_9}), .b(in_15), .eq(comparator_2_eq));  // open: gt, lt
  and and_1 (e1_e2, comparator_1_eq, comparator_2_eq);
endmodule

module circuit_de_Controle (
  input  Resultat_de_multiplication_des_comparateurs,
  input  RESET_for_ALARME,
  output Q,
  output nQ
);

  S_R_Flip_Flop #(.trigger("high")) s_r_ff_1 (
    .S(Resultat_de_multiplication_des_comparateurs), .clk(1'b1), .R(RESET_for_ALARME), .Q(Q), .Qn(nQ));  // open: preset, reset, en
endmodule

module circuit_de_seconde_et_minute (
  input  CLK,
  input  nqcontrole1,
  input  nqcontrole2,
  input  qcontrole1,
  input  _0,
  input  in_6,
  input  qcontrole2,
  input  in_8,
  input  in_9,
  input  in_10,
  input  in_11,
  input  in_12,
  input  in_13,
  input  in_14,
  input  in_15,
  input  in_16,
  input  in_17,
  input  in_18,
  input  in_19,
  input  _8,
  input  in_21,
  output [3:0] screen2,
  output [3:0] screen1,
  output output_pour_la_seconde_circuit,
  output e1_e2
);

  wire and_2_out, comparateur_et_encodeur_1_1_e_5, comparateur_et_encodeur_1_1_e_9,
       comparateur_et_encodeur_1_1_q0_5, comparateur_et_encodeur_1_1_q0_9, comparateur_et_encodeur_1_1_q1_5,
       comparateur_et_encodeur_1_1_q1_9, comparateur_et_encodeur_1_1_q2_5, comparateur_et_encodeur_1_1_q2_9,
       comparateur_et_encodeur_1_1_q3_9, compteur_synchrone_modulo_6_1_nq0_6,
       compteur_synchrone_modulo_6_1_nq1_6, compteur_synchrone_modulo_6_1_nq2_6,
       compteur_synchrone_modulo_10_1_nq0_10, compteur_synchrone_modulo_10_1_nq1_10,
       compteur_synchrone_modulo_10_1_nq2_10, compteur_synchrone_modulo_10_1_nq2_10_2;
  wire [2:0] compteur_synchrone_modulo_6_1_q0_6;
  wire [3:0] compteur_synchrone_modulo_10_1_q0_10;

  Alarm2 alarm2_1 (
    .q0B(compteur_synchrone_modulo_6_1_q0_6[0]), .nqcontrol(nqcontrole1), .CLK(CLK), .qcontrol(qcontrole1),
    .q0encodeur(comparateur_et_encodeur_1_1_q0_5), .q1B(compteur_synchrone_modulo_6_1_q0_6[1]),
    .nqcontrol_2(nqcontrole1), .CLK_2(CLK), .qcontrol_2(qcontrole1),
    .q1encodeur(comparateur_et_encodeur_1_1_q1_5), .q2B(compteur_synchrone_modulo_6_1_q0_6[2]),
    .nqcontrol_3(nqcontrole1), .CLK_3(CLK), .qcontrol_3(qcontrole1),
    .q2encodeur(comparateur_et_encodeur_1_1_q2_5), ._0(screen2[0]), ._1(screen2[1]), ._2(screen2[2]));
  and and_1 (output_pour_la_seconde_circuit, compteur_synchrone_modulo_6_1_nq0_6, compteur_synchrone_modulo_6_1_nq1_6, compteur_synchrone_modulo_6_1_nq2_6);
  compteur_synchrone_modulo_6 compteur_synchrone_modulo_6_1 (
    .CLK(and_2_out), .q0_6(compteur_synchrone_modulo_6_1_q0_6[0]),
    .q1_6(compteur_synchrone_modulo_6_1_q0_6[1]), .q2_6(compteur_synchrone_modulo_6_1_q0_6[2]),
    .nq0_6(compteur_synchrone_modulo_6_1_nq0_6), .nq1_6(compteur_synchrone_modulo_6_1_nq1_6),
    .nq2_6(compteur_synchrone_modulo_6_1_nq2_6));
  and and_2 (and_2_out, compteur_synchrone_modulo_10_1_nq0_10, compteur_synchrone_modulo_10_1_nq1_10, compteur_synchrone_modulo_10_1_nq2_10, compteur_synchrone_modulo_10_1_nq2_10_2);
  Comparateur_et_Encodeur_1 comparateur_et_encodeur_1_1 (
    ._0(_0), ._1(in_6), ._2(in_8), ._3(in_9), ._4(in_10), ._5(in_11), ._0_2(in_12), ._1_2(in_13),
    ._2_2(in_14), ._3_2(in_15), ._4_2(in_16), ._5_2(in_17), ._6(in_18), ._7(in_19), ._8(_8), ._9(in_21),
    .in_1(compteur_synchrone_modulo_6_1_q0_6), .in_18(compteur_synchrone_modulo_10_1_q0_10),
    .q0_5(comparateur_et_encodeur_1_1_q0_5), .q1_5(comparateur_et_encodeur_1_1_q1_5),
    .e_5(comparateur_et_encodeur_1_1_e_5), .q2_5(comparateur_et_encodeur_1_1_q2_5),
    .q0_9(comparateur_et_encodeur_1_1_q0_9), .q1_9(comparateur_et_encodeur_1_1_q1_9),
    .q2_9(comparateur_et_encodeur_1_1_q2_9), .e_9(comparateur_et_encodeur_1_1_e_9),
    .q3_9(comparateur_et_encodeur_1_1_q3_9));
  compteur_synchrone_modulo_10 compteur_synchrone_modulo_10_1 (
    .CLK(CLK), .q0_10(compteur_synchrone_modulo_10_1_q0_10[0]),
    .q1_10(compteur_synchrone_modulo_10_1_q0_10[1]), .q2_10(compteur_synchrone_modulo_10_1_q0_10[2]),
    .q3_10(compteur_synchrone_modulo_10_1_q0_10[3]), .nq0_10(compteur_synchrone_modulo_10_1_nq0_10),
    .nq1_10(compteur_synchrone_modulo_10_1_nq1_10), .nq2_10(compteur_synchrone_modulo_10_1_nq2_10),
    .nq2_10_2(compteur_synchrone_modulo_10_1_nq2_10_2));  // open: RESET
  Alaram1 alaram1_1 (
    .q0B(compteur_synchrone_modulo_10_1_q0_10[0]), .nqcontrol(nqcontrole2), .CLK(CLK), .qcontrol(qcontrole2),
    .q0encodeur(comparateur_et_encodeur_1_1_q0_9), .q1B(compteur_synchrone_modulo_10_1_q0_10[1]),
    .nqcontrol_2(nqcontrole2), .CLK_2(CLK), .qcontrol_2(qcontrole2),
    .q1encodeur(comparateur_et_encodeur_1_1_q1_9), .q2B(compteur_synchrone_modulo_10_1_q0_10[2]),
    .nqcontrol_3(nqcontrole2), .CLK_3(CLK), .qcontrol_3(qcontrole2),
    .q2encodeur(comparateur_et_encodeur_1_1_q2_9), .q3B(compteur_synchrone_modulo_10_1_q0_10[3]),
    .nqcontrol_4(nqcontrole2), .CLK_4(CLK), .qcontrol_4(qcontrole2),
    .q3encodeur(comparateur_et_encodeur_1_1_q3_9), ._0(screen1[0]), ._1(screen1[1]), ._2(screen1[2]),
    ._3(screen1[3]));
  and and_3 (e1_e2, comparateur_et_encodeur_1_1_e_5, comparateur_et_encodeur_1_1_e_9);

  assign screen2[3] = 1'b0;
endmodule

module circuit_d_heure (
  input  nqControl,
  input  CLK,
  input  qControl,
  input  in_4,
  input  in_5,
  input  in_6,
  input  in_7,
  input  in_8,
  input  in_9,
  input  in_10,
  input  in_11,
  input  in_12,
  input  in_13,
  input  in_14,
  input  in_15,
  input  in_16,
  output [3:0] screen1,
  output [3:0] screen2,
  output e1_e2
);

  wire and_1_out, and_2_out, and_3_out, comparateur_et_encodeur_2_1_q0_2, comparateur_et_encodeur_2_1_q0_9,
       comparateur_et_encodeur_2_1_q1_2, comparateur_et_encodeur_2_1_q1_9, comparateur_et_encodeur_2_1_q2_9,
       comparateur_et_encodeur_2_1_q3_9, compteur_synchrone_modulo_10_1_nq0_10,
       compteur_synchrone_modulo_10_1_nq1_10, compteur_synchrone_modulo_10_1_nq2_10,
       compteur_synchrone_modulo_10_1_nq2_10_2, comteur_synchrone_modulo_3_1_nq0_3;
  wire [1:0] comteur_synchrone_modulo_3_1_q0_3;
  wire [3:0] compteur_synchrone_modulo_10_1_q0_10;

  Alarm3 alarm3_1 (
    .q0B(comteur_synchrone_modulo_3_1_q0_3[0]), .nqcontrol(nqControl), .CLK(CLK), .qcontrol(qControl),
    .q0encodeur(comparateur_et_encodeur_2_1_q0_2), .q1B(comteur_synchrone_modulo_3_1_q0_3[1]),
    .nqcontrol_2(nqControl), .CLK_2(CLK), .qcontrol_2(qControl),
    .q1encodeur(comparateur_et_encodeur_2_1_q1_2), ._0(screen2[0]), ._1(screen2[1]));
  comteur_synchrone_modulo_3 comteur_synchrone_modulo_3_1 (
    .CLK(and_2_out), .q0_3(comteur_synchrone_modulo_3_1_q0_3[0]),
    .q1_3(comteur_synchrone_modulo_3_1_q0_3[1]), .nq0_3(comteur_synchrone_modulo_3_1_nq0_3), .RESET(and_1_out));  // open: nq1_3
  and and_1 (and_1_out, comteur_synchrone_modulo_3_1_q0_3[0], comteur_synchrone_modulo_3_1_q0_3[1]);
  and and_2 (and_2_out, compteur_synchrone_modulo_10_1_nq0_10, compteur_synchrone_modulo_10_1_nq1_10, compteur_synchrone_modulo_10_1_nq2_10, compteur_synchrone_modulo_10_1_nq2_10_2);
  compteur_synchrone_modulo_10 compteur_synchrone_modulo_10_1 (
    .CLK(CLK), .q0_10(compteur_synchrone_modulo_10_1_q0_10[0]),
    .q1_10(compteur_synchrone_modulo_10_1_q0_10[1]), .q2_10(compteur_synchrone_modulo_10_1_q0_10[2]),
    .q3_10(compteur_synchrone_modulo_10_1_q0_10[3]), .nq0_10(compteur_synchrone_modulo_10_1_nq0_10),
    .nq1_10(compteur_synchrone_modulo_10_1_nq1_10), .nq2_10(compteur_synchrone_modulo_10_1_nq2_10),
    .nq2_10_2(compteur_synchrone_modulo_10_1_nq2_10_2), .RESET(and_3_out));
  and and_3 (and_3_out, compteur_synchrone_modulo_10_1_q0_10[0], compteur_synchrone_modulo_10_1_q0_10[2], comteur_synchrone_modulo_3_1_q0_3[1], comteur_synchrone_modulo_3_1_nq0_3, compteur_synchrone_modulo_10_1_nq2_10_2, compteur_synchrone_modulo_10_1_nq1_10);
  Alaram1 alaram1_1 (
    .q0B(compteur_synchrone_modulo_10_1_q0_10[0]), .nqcontrol(nqControl), .CLK(CLK), .qcontrol(qControl),
    .q0encodeur(comparateur_et_encodeur_2_1_q0_9), .q1B(compteur_synchrone_modulo_10_1_q0_10[1]),
    .nqcontrol_2(nqControl), .CLK_2(CLK), .qcontrol_2(qControl),
    .q1encodeur(comparateur_et_encodeur_2_1_q1_9), .q2B(compteur_synchrone_modulo_10_1_q0_10[2]),
    .nqcontrol_3(nqControl), .CLK_3(CLK), .qcontrol_3(qControl),
    .q2encodeur(comparateur_et_encodeur_2_1_q2_9), .q3B(compteur_synchrone_modulo_10_1_q0_10[3]),
    .nqcontrol_4(nqControl), .CLK_4(CLK), .qcontrol_4(qControl),
    .q3encodeur(comparateur_et_encodeur_2_1_q3_9), ._0(screen1[0]), ._1(screen1[1]), ._2(screen1[2]),
    ._3(screen1[3]));
  Comparateur_et_Encodeur_2 comparateur_et_encodeur_2_1 (
    ._0(in_4), ._1(in_5), ._2(in_6), ._0_2(in_7), ._1_2(in_8), ._2_2(in_9), ._3(in_10), ._4(in_11),
    ._5(in_12), ._6(in_13), ._7(in_14), ._8(in_15), ._9(in_16), .in_1(comteur_synchrone_modulo_3_1_q0_3),
    .in_15(compteur_synchrone_modulo_10_1_q0_10), .q0_2(comparateur_et_encodeur_2_1_q0_2),
    .q1_2(comparateur_et_encodeur_2_1_q1_2), .e1_e2(e1_e2), .q0_9(comparateur_et_encodeur_2_1_q0_9),
    .q1_9(comparateur_et_encodeur_2_1_q1_9), .q2_9(comparateur_et_encodeur_2_1_q2_9),
    .q3_9(comparateur_et_encodeur_2_1_q3_9));

  assign screen2[3:2] = 2'b00;
endmodule

module Alarm3 (
  input  q0B,
  input  nqcontrol,
  input  CLK,
  input  qcontrol,
  input  q0encodeur,
  input  q1B,
  input  nqcontrol_2,
  input  CLK_2,
  input  qcontrol_2,
  input  q1encodeur,
  output _0,
  output _1
);

  wire and_1_out, and_2_out, and_3_out, and_4_out;

  and and_1 (and_1_out, q0B, nqcontrol);
  and and_2 (and_2_out, CLK, qcontrol, q0encodeur);
  and and_3 (and_3_out, q1B, nqcontrol_2);
  and and_4 (and_4_out, CLK_2, qcontrol_2, q1encodeur);
  or or_1 (_0, and_1_out, and_2_out);
  or or_2 (_1, and_3_out, and_4_out);
endmodule
